// Logisim project Exercicio01-Decoder1035.circ as structural Verilog: 1 circuit, main circuit main
module main (
  input  in_1,
  input  in_2,
  input  in_3,
  input  in_4,
  input  in_5,
  input  in_6,
  input  in_7,
  input  in_8,
  input  in_9,
  input  in_10,
  input  in_11,
  input  in_12,
  input  in_13,
  input  in_14,
  input  in_15,
  input  in_16,
  output out_17
);

  wire not_1_out, not_2_out, not_3_out, not_4_out, not_5_out, not_6_out, not_7_out, not_8_out, not_9_out,
       not_10_out, not_11_out, not_12_out;

  not not_1 (not_1_out, in_1);
  not not_2 (not_2_out, in_2);
  not not_3 (not_3_out, in_3);
  not not_4 (not_4_out, in_4);
  not not_5 (not_5_out, in_5);
  not not_6 (not_6_out, in_7);
  not not_7 (not_7_out, in_8);
  and and_1 (out_17, not_1_out, not_2_out, not_3_out, not_4_out, not_5_out, in_6, not_6_out, not_7_out, not_8_out, not_9_out, not_10_out, not_11_out, in_13, not_12_out, in_15, in_16);
  not not_8 (not_8_out, in_9);
  not not_9 (not_9_out, in_10);
  not not_10 (not_10_out, in_11);
  not not_11 (not_11_out, in_12);
  not not_12 (not_12_out, in_14);
endmodule
